# Fritzing sketch slider v1 (saved by Fritzing 0.9.3b)
breadboards: 1

parts:
  arduino_nano = Arduino Nano (Rev3.0)
  oled_128x32 = OLED Monochrome 128x32 I2C [part_number=931]
  LED3_mov = LED - 3mm [color="Red (633nm)" package="3 mm [THT]"]
  LED4_espera = LED - 3mm [color="Red (633nm)" package="3 mm [THT]"]
  BREAKOUT1 = ULN2003A breakout board
  Q1 = PNP-Transistor [package="TO92 [THT]"]
  JP2 = Header 3 [package=screwterminal-3.5mm-3_lock.007s]
  Q2 = PNP-Transistor [package="TO92 [THT]"]
  DE = SWITCH-MOMENTARY-2 [package=tactile-pth-12mm]
  IZ = SWITCH-MOMENTARY-2 [package=tactile-pth-12mm]
  OK = SWITCH-MOMENTARY-2 [package=tactile-pth-12mm]
  LED3_mov1 = LED - 3mm [color="Red (633nm)" package="3 mm [THT]"]
  LED4_espera1 = LED - 3mm [color="Red (633nm)" package="3 mm [THT]"]
  R7_boton_OK = Resistor [tolerance=±5% resistance=220 package=THT]
  R8_botonIZ = Resistor [tolerance=±5% resistance=220 package=THT]
  R9_boton_DE = Resistor [tolerance=±5% resistance=220 package=THT]
  R10_Led_focus = Resistor [tolerance=±5% resistance=220 package=THT]
  R11_tr_focus = Resistor [tolerance=±5% resistance=220 package=THT]
  R12_tr_disp = Resistor [tolerance=±5% resistance=220 package=THT]
  R13_led_disp = Resistor [tolerance=±5% resistance=220 package=THT]
  R14_led_mov = Resistor [tolerance=±5% resistance=220 package=THT]
  R15_led_espera = Resistor [tolerance=±5% resistance=220 package=THT]
  JP3 = Header 4 [package=screwterminal-3.5mm-4_lock]

nets:
  GND: arduino_nano.GND, oled_128x32.GND, Q1.E, JP2.2, Q2.E, LED3_mov1.cathode, LED4_espera1.cathode, R7_boton_OK.Pin_0, R8_botonIZ.Pin_0, R9_boton_DE.Pin_0
  N1: arduino_nano.D2, OK.1, R7_boton_OK.Pin_1
  N2: arduino_nano.D3, IZ.1, R8_botonIZ.Pin_1
  N3: arduino_nano.D4, DE.1, R9_boton_DE.Pin_1
  N4: arduino_nano.D5, R10_Led_focus.Pin_1, R11_tr_focus.Pin_0
  N5: arduino_nano.D8, JP3.4
  N6: arduino_nano.D9, JP3.3
  N7: arduino_nano.D10, JP3.2
  N8: arduino_nano.D11/MOSI, JP3.1
  5V: arduino_nano.5V, oled_128x32.VIN, DE.2, IZ.2, OK.2
  N9: arduino_nano.A5, oled_128x32.SCL
  N10: arduino_nano.A4, oled_128x32.SDA
  N11: arduino_nano.A1, R14_led_mov.Pin_1
  N12: arduino_nano.A0, R15_led_espera.Pin_1
  N13: LED3_mov.cathode, LED4_espera.cathode
  N14: LED3_mov.anode, R14_led_mov.Pin_0
  N15: LED4_espera.anode, R15_led_espera.Pin_0
  N16: BREAKOUT1.0V, BREAKOUT1.+5V, BREAKOUT1.ON/OFF_jumper_switch
  N17: Q1.B, R11_tr_focus.Pin_1
  N18: Q1.C, JP2.3
  N19: JP2.1, Q2.C
  N20: Q2.B, R12_tr_disp.Pin_1
  N21: LED3_mov1.anode, R13_led_disp.Pin_1
  N22: LED4_espera1.anode, R10_Led_focus.Pin_0
  N23: R12_tr_disp.Pin_0, R13_led_disp.Pin_0

custom parts:
  OLED Monochrome 128x32 I2C: These displays are small, only about 1" diagonal, but very readable due to the high contrast of an OLED display. This display is made of 128x32 individual white OLED pixels, each one is turned on or off by the controller chip. Because the display makes its own light, no backlight is required. This reduces the power required to run the OLED and is why the display has such high contrast; we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
  ULN2003A breakout board: ULN2003A 7-way Darlington Transistor Driver on breakoutboard
