# Fritzing sketch slider v1 (saved by Fritzing 0.9.3b)
breadboards: 1

parts:
  arduino_nano = Arduino Nano (Rev3.0)
  oled_128x32 = OLED Monochrome 128x32 I2C [part_number=931]
  R1 = Resistor [tolerance=±5% resistance=220 package="0805 [SMD]"]
  R2 = Resistor [tolerance=±5% resistance=220 package="0805 [SMD]"]
  LED3_mov = LED - 3mm [color="Red (633nm)" package="3 mm [THT]"]
  LED4_espera = LED - 3mm [color="Red (633nm)" package="3 mm [THT]"]
  BREAKOUT1 = ULN2003A breakout board  # not connected
  JP1 = Header 4 [package=jst-4-pth]
  R3 = Resistor [tolerance=±5% resistance=220 package="0805 [SMD]"]
  Q1 = PNP-Transistor [package="TO92 [THT]"]
  JP2 = Header 3 [package=screwterminal-3.5mm-3_lock.007s]
  Q2 = PNP-Transistor [package="TO92 [THT]"]
  DE = SWITCH-MOMENTARY-2 [package=tactile-pth-12mm]
  IZ = SWITCH-MOMENTARY-2 [package=tactile-pth-12mm]
  OK = SWITCH-MOMENTARY-2 [package=tactile-pth-12mm]
  R4_DE = Resistor [tolerance=±5% resistance=220 package="0805 [SMD]"]
  R5_IZ = Resistor [tolerance=±5% resistance=220 package="0805 [SMD]"]
  R6_OK = Resistor [tolerance=±5% resistance=220 package="0805 [SMD]"]
  R4 = Resistor [tolerance=±5% resistance=220 package="0805 [SMD]"]
  R5 = Resistor [tolerance=±5% resistance=220 package="0805 [SMD]"]
  LED3_mov1 = LED - 3mm [color="Red (633nm)" package="3 mm [THT]"]
  LED4_espera1 = LED - 3mm [color="Red (633nm)" package="3 mm [THT]"]
  R6 = Resistor [tolerance=±5% resistance=220 package="0805 [SMD]"]

nets (from the schematic view):
  GND: arduino_nano.GND, oled_128x32.GND, Q1.E, JP2.2, Q2.E, R4_DE.Pin_0, R5_IZ.Pin_0, R6_OK.Pin_0, LED3_mov1.cathode, LED4_espera1.cathode
  N1: arduino_nano.D2, OK.1, R6_OK.Pin_1
  N2: arduino_nano.D3, IZ.1, R5_IZ.Pin_1
  N3: arduino_nano.D4, DE.1, R4_DE.Pin_1
  N4: arduino_nano.D5, R3.Pin_0, R4.Pin_1
  N5: arduino_nano.D6, R5.Pin_1, R6.Pin_0
  N6: arduino_nano.D8, JP1.4
  N7: arduino_nano.D9, JP1.3
  N8: arduino_nano.D10, JP1.2
  N9: arduino_nano.D11/MOSI, JP1.1
  5V: arduino_nano.5V, oled_128x32.VIN, DE.2, IZ.2, OK.2
  N10: arduino_nano.A5, oled_128x32.SCL
  N11: arduino_nano.A4, oled_128x32.SDA
  N12: arduino_nano.A1, R2.Pin_1
  N13: arduino_nano.A0, R1.Pin_1
  N14: R1.Pin_0, LED4_espera.anode
  N15: R2.Pin_0, LED3_mov.anode
  N16: LED3_mov.cathode, LED4_espera.cathode
  N17: R3.Pin_1, Q1.B
  N18: Q1.C, JP2.3
  N19: JP2.1, Q2.C
  N20: Q2.B, R6.Pin_1
  N21: R4.Pin_0, LED4_espera1.anode
  N22: R5.Pin_0, LED3_mov1.anode

custom parts:
  OLED Monochrome 128x32 I2C: These displays are small, only about 1" diagonal, but very readable due to the high contrast of an OLED display. This display is made of 128x32 individual white OLED pixels, each one is turned on or off by the controller chip. Because the display makes its own light, no backlight is required. This reduces the power required to run the OLED and is why the display has such high contrast; we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
  ULN2003A breakout board: ULN2003A 7-way Darlington Transistor Driver on breakoutboard
